# Fritzing sketch fritzing (saved by Fritzing 0.9.5d)
breadboards: 1

parts:
  Компонент1 = Arduino Nano (Rev3.0)
  TM1 = TM1637 Display
  Encoder_round1 = Encoder round
  Module1 = Relay
  Thermistor1 = Thermistor
  R1 = Resistor [tolerance=±5% resistance=10k package=THT]

nets:
  N1: Компонент1.D2, Module1.signal
  N2: Компонент1.D3, Encoder_round1.pin4
  N3: Компонент1.D4, Encoder_round1.pin3
  N4: Компонент1.D5, Encoder_round1.pin2
  N5: Компонент1.D11/MOSI, TM1.pin1
  N6: Компонент1.D12/MISO, TM1.pin2
  N7: Компонент1.A0, Thermistor1.pin2, R1.Pin_0
  N8: TM1.pin3, Encoder_round1.pin5, Module1.power
  N9: TM1.pin4, Encoder_round1.pin1, Module1.ground, Thermistor1.pin1, R1.Pin_1
